// Logisim project 4.circ as structural Verilog: 2 circuits, main circuit 4bit_swap
module swap (
  input  I1,
  input  I2,
  input  S,
  output O1,
  output O2
);

  wire and_1_out, and_2_out, and_3_out, and_4_out, and_5_out, not_1_out, not_2_out;

  not not_1 (not_1_out, S);
  not not_2 (not_2_out, S);
  and and_1 (and_1_out, I2, S);
  and and_2 (and_2_out, I1, not_1_out);
  and and_3 (and_3_out, I1, S);
  and and_4 (and_4_out, I2, I1);
  and and_5 (and_5_out, I2, not_2_out);
  or or_1 (O1, and_1_out, and_2_out, and_4_out);
  or or_2 (O2, and_4_out, and_5_out, and_3_out);
endmodule

module _4bit_swap (
  input  [3:0] in_1,
  input  [3:0] in_2,
  input  in_3,
  output [3:0] out_4,
  output [3:0] out_5
);

  swap swap_1 (.I1(in_1[0]), .I2(in_2[0]), .S(in_3), .O1(out_4[0]), .O2(out_5[0]));
  swap swap_2 (.I1(in_1[1]), .I2(in_2[1]), .S(in_3), .O1(out_4[1]), .O2(out_5[1]));
  swap swap_3 (.I1(in_1[2]), .I2(in_2[2]), .S(in_3), .O1(out_4[2]), .O2(out_5[2]));
  swap swap_4 (.I1(in_1[3]), .I2(in_2[3]), .S(in_3), .O1(out_4[3]), .O2(out_5[3]));
endmodule
