// Logisim project Arth Right.circ as structural Verilog: 1 circuit, main circuit main
module main (
  input  [15:0] in_1,
  input  [3:0] in_2,
  output [15:0] out_3
);

  wire a;
  wire [3:0] demultiplexer_3_out1;
  wire [15:0] demultiplexer_1_out0, demultiplexer_1_out1, demultiplexer_2_out0, demultiplexer_2_out1,
       demultiplexer_3_out0, demultiplexer_3_out1_2, demultiplexer_4_out0, demultiplexer_4_out1, or_1_out,
       or_2_out, or_3_out;
  wire [15:15] and_2_out, and_3_out, and_5_out;

  Demultiplexer #(.width(16)) demultiplexer_1 (
    .out0(demultiplexer_1_out0), .out1(demultiplexer_1_out1), .in(in_1), .sel(in_2[0]));  // open: en
  and and_1 (a, 1'b1, in_1[15]);
  and and_2 (and_2_out[15], a, in_2[0]);
  Demultiplexer #(.width(16)) demultiplexer_2 (
    .out0(demultiplexer_2_out0), .out1(demultiplexer_2_out1), .in(or_1_out), .sel(in_2[1]));  // open: en
  assign or_1_out = {and_2_out[15], demultiplexer_1_out1[15:1]} | demultiplexer_1_out0;  // OR_Gate or_1, 16 bits wide
  and and_3 (and_3_out[15], a, in_2[1]);
  and and_4 (demultiplexer_3_out1_2[15], a, in_2[2]);
  assign or_2_out = {{2{and_3_out[15]}}, demultiplexer_2_out1[15:2]} | demultiplexer_2_out0;  // OR_Gate or_2, 16 bits wide
  Demultiplexer #(.width(16)) demultiplexer_3 (
    .out0(demultiplexer_3_out0), .out1({demultiplexer_3_out1_2[11:0], demultiplexer_3_out1}), .in(or_2_out),
    .sel(in_2[2]));  // open: en
  assign or_3_out = {{4{demultiplexer_3_out1_2[15]}}, demultiplexer_3_out1_2[11:0]} | demultiplexer_3_out0;  // OR_Gate or_3, 16 bits wide
  and and_5 (and_5_out[15], a, in_2[3]);
  Demultiplexer #(.width(16)) demultiplexer_4 (
    .out0(demultiplexer_4_out0), .out1(demultiplexer_4_out1), .in(or_3_out), .sel(in_2[3]));  // open: en
  assign out_3 = {{8{and_5_out[15]}}, demultiplexer_4_out1[15:8]} | demultiplexer_4_out0;  // OR_Gate or_4, 16 bits wide
endmodule
