// Logisim project Fib.circ as structural Verilog: 1 circuit, main circuit main
module main (
  input  [2:0] N,
  output [3:0] Nth
);

  wire clo, comparator_1_lt, counter_2_q, not_1_out;
  wire [3:0] adder_1_out, bit_extender_1_out, counter_1_q, multiplexer_1_out, p, register_2_q;

  Clock clock_1 (.out(clo));
  assign bit_extender_1_out = {{1{1'b0}}, N};  // Bit_Extender bit_extender_1
  Counter #(.width(4), .max('hf), .ongoal("stay")) counter_1 (
    .Q(counter_1_q), .clk(clo));  // open: load, D, count, carry, clr
  // Probe on counter_1_q
  Comparator #(.width(4), .mode("unsigned")) comparator_1 (
    .a(bit_extender_1_out), .b(counter_1_q), .lt(comparator_1_lt));  // open: gt, eq
  not not_1 (not_1_out, comparator_1_lt);
  Counter #(.width(1), .max('h1), .ongoal("stay")) counter_2 (
    .Q(counter_2_q), .clk(clo));  // open: load, D, count, carry, clr
  Multiplexer #(.width(4)) multiplexer_1 (
    .in0(4'b0001), .in1(register_2_q), .out(multiplexer_1_out), .sel(counter_2_q));  // open: en
  Register #(.width(4)) register_1 (.D(multiplexer_1_out), .en(not_1_out), .Q(p), .clk(clo));  // open: clr
  // Probe on p
  // Probe on adder_1_out
  Adder #(.width(4)) adder_1 (.a(register_2_q), .b(p), .out(adder_1_out));  // open: cin, cout
  Register #(.width(4)) register_2 (.D(adder_1_out), .en(not_1_out), .Q(register_2_q), .clk(clo));  // open: clr
  // Probe on register_2_q
  Multiplexer #(.width(4)) multiplexer_2 (
    .in0(4'b0000), .in1(register_2_q), .out(Nth), .sel(comparator_1_lt));  // open: en
endmodule
