// Logisim project Tran.circ as structural Verilog
module Tran (
  input  C0,
  input  C1,
  input  b,
  output out_4,
  output out_5
);

  wire and_1_out, and_2_out, and_3_out, and_4_out, and_5_out, and_6_out, not_1_out, not_2_out, not_3_out,
       not_4_out, not_5_out, not_6_out, not_7_out, not_8_out;

  not not_1 (not_1_out, C0);
  not not_2 (not_2_out, C1);
  not not_3 (not_3_out, C0);
  not not_4 (not_4_out, C1);
  not not_5 (not_5_out, C0);
  not not_6 (not_6_out, b);
  not not_7 (not_7_out, C1);
  not not_8 (not_8_out, b);
  and and_1 (and_1_out, not_1_out, C1);
  and and_2 (and_2_out, C0, not_2_out);
  and and_3 (and_3_out, not_3_out, not_4_out, b);
  and and_4 (and_4_out, not_5_out, C1, not_6_out);
  and and_5 (and_5_out, C0, not_7_out, not_8_out);
  and and_6 (and_6_out, C0, C1, b);
  or or_1 (out_4, and_1_out, and_2_out);
  or or_2 (out_5, and_3_out, and_4_out, and_5_out, and_6_out);
endmodule

module mod5 (
  input  In,
  output S0,
  output S1,
  output S2,
  output S3,
  output S4
);

  wire and_1_out, and_2_out, and_3_out, and_4_out, and_5_out, and_6_out, and_7_out, and_8_out, clock_1_out,
       not_1_out, not_2_out, not_3_out, not_4_out, not_5_out, not_6_out, not_7_out, not_8_out, not_9_out,
       not_10_out, not_11_out, not_12_out;
  wire [1:0] register_1_q, tran_1_out_4;

  Tran tran_1 (.C0(register_1_q[0]), .C1(register_1_q[1]), .b(In), .out_4(tran_1_out_4[0]), .out_5(tran_1_out_4[1]));
  Clock clock_1 (.out(clock_1_out));
  Register #(.width(2)) register_1 (.D(tran_1_out_4), .Q(register_1_q), .clk(clock_1_out));  // open: en, clr
  not not_1 (not_1_out, register_1_q[0]);
  not not_2 (not_2_out, register_1_q[1]);
  not not_3 (not_3_out, In);
  not not_4 (not_4_out, In);
  not not_5 (not_5_out, register_1_q[0]);
  not not_6 (not_6_out, register_1_q[1]);
  not not_7 (not_7_out, register_1_q[0]);
  not not_8 (not_8_out, register_1_q[1]);
  not not_9 (not_9_out, register_1_q[0]);
  not not_10 (not_10_out, In);
  not not_11 (not_11_out, register_1_q[1]);
  not not_12 (not_12_out, In);
  and and_1 (and_1_out, not_1_out, not_2_out, not_3_out);
  and and_2 (and_2_out, register_1_q[0], register_1_q[1], not_4_out);
  and and_3 (and_3_out, not_5_out, not_6_out, In);
  and and_4 (and_4_out, register_1_q[0], register_1_q[1], In);
  and and_5 (and_5_out, not_7_out, register_1_q[1], In);
  and and_6 (and_6_out, register_1_q[0], not_8_out, In);
  and and_7 (and_7_out, not_9_out, register_1_q[1], not_10_out);
  and and_8 (and_8_out, register_1_q[0], not_11_out, not_12_out);
  or or_1 (S1, and_1_out, and_2_out);
  or or_2 (S2, and_3_out, and_4_out);
  or or_3 (S3, and_5_out, and_6_out);
  or or_4 (S4, and_7_out, and_8_out);

  assign S0 = 1'b0;
endmodule
