// Logisim project crc校验.circ as structural Verilog: 2 circuits, main circuit CRC
module CRC (
  input  [7:0] in_1,
  input  [3:0] in_2,
  output [10:0] out_3
);

  wire [2:0] _3, \四位模2_1_out_3 , \四位模2_2_out_3 , \四位模2_3_out_3 , \四位模2_4_out_3 , \四位模2_5_out_3 ;
  wire [3:1] \四位模2_7_out_3 ;

  \四位模2  \u_四位模2_1  (.\被除数 (in_1[7:4]), .\除数 (in_2), .out_3(\四位模2_1_out_3 ));
  \四位模2  \u_四位模2_2  (.\被除数 ({_3, 1'b0}), .\除数 (in_2), .out_3(\四位模2_2_out_3 ));
  \四位模2  \u_四位模2_3  (.\被除数 ({\四位模2_1_out_3 , in_1[3]}), .\除数 (in_2), .out_3(\四位模2_3_out_3 ));
  \四位模2  \u_四位模2_4  (.\被除数 ({\四位模2_2_out_3 , 1'b0}), .\除数 (in_2), .out_3(\四位模2_4_out_3 ));
  \四位模2  \u_四位模2_5  (.\被除数 ({\四位模2_3_out_3 , in_1[2]}), .\除数 (in_2), .out_3(\四位模2_5_out_3 ));
  \四位模2  \u_四位模2_6  (.\被除数 ({\四位模2_4_out_3 , 1'b0}), .\除数 (in_2), .out_3(out_3[2:0]));
  \四位模2  \u_四位模2_7  (.\被除数 ({\四位模2_5_out_3 , in_1[1]}), .\除数 (in_2), .out_3(\四位模2_7_out_3 ));
  \四位模2  \u_四位模2_8  (.\被除数 ({\四位模2_7_out_3 , in_1[0]}), .\除数 (in_2), .out_3(_3));

  assign out_3[10:3] = in_1;

  // Other names for the same wires on the sheet: cs[3:0] = in_2
endmodule

module \四位模2  (
  input  [3:0] \被除数 ,
  input  [3:0] \除数 ,
  output [2:0] out_3
);

  wire comparator_1_eq;
  wire [3:0] _1, multiplexer_1_out;

  assign _1 = \被除数  ^ \除数 ;  // XOR_Gate xor_1, 4 bits wide
  Multiplexer #(.width(4)) multiplexer_1 (
    .in0(\被除数 ), .in1(_1), .out(multiplexer_1_out), .sel(comparator_1_eq));  // open: en
  Comparator #(.width(1)) comparator_1 (.a(\被除数 [3]), .b(1'b1), .eq(comparator_1_eq));  // open: gt, lt
  Bit_Extender #(.in_width(4), .out_width(3)) bit_extender_1 (.in(multiplexer_1_out), .out(out_3));
endmodule
