// Logisim project fib2.circ as structural Verilog: 8 circuits, main circuit main
module main (
  input  [31:0] in_1,
  output [31:0] out_2
);

  wire \计数_1_out_2 , \计数_1_out_3 ;

  \计数  \u_计数_1  (.in_1(in_1), .out_2(\计数_1_out_2 ), .out_3(\计数_1_out_3 ));
  \计算  \u_计算_1  (.in_1(\计数_1_out_2 ), .in_2(\计数_1_out_3 ), .out_3(out_2));
endmodule

module \寄存器矩阵  (
  input  [31:0] a11_in,
  input  [31:0] a12_in,
  input  [31:0] a13_in,
  input  [31:0] a14_in,
  input  ena,
  input  clk,
  output [31:0] a11_out,
  output [31:0] a12_out,
  output [31:0] a21_OUT,
  output [31:0] a22_out
);

  Register #(.width(32)) register_1 (.D(a11_in), .en(ena), .Q(a11_out), .clk(clk));  // open: clr
  Register #(.width(32)) register_2 (.D(a12_in), .en(ena), .Q(a12_out), .clk(clk));  // open: clr
  Register #(.width(32)) register_3 (.D(a13_in), .en(ena), .Q(a21_OUT), .clk(clk));  // open: clr
  Register #(.width(32)) register_4 (.D(a14_in), .en(ena), .Q(a22_out), .clk(clk));  // open: clr
endmodule

module multi (
  input  [31:0] in_1,
  input  [31:0] in_2,
  input  [31:0] in_3,
  input  [31:0] in_4,
  input  [31:0] in_5,
  input  [31:0] in_6,
  input  [31:0] in_7,
  input  [31:0] in_8,
  output [31:0] out_9,
  output [31:0] out_10,
  output [31:0] out_11,
  output [31:0] out_12
);

  wire [31:0] multiplier_1_out, multiplier_2_out, multiplier_3_out, multiplier_4_out, multiplier_5_out,
       multiplier_6_out, multiplier_7_out, multiplier_8_out;

  Multiplier #(.width(32)) multiplier_1 (.a(in_1), .b(in_5), .out(multiplier_1_out));  // open: cin, cout
  Multiplier #(.width(32)) multiplier_2 (.a(in_2), .b(in_7), .out(multiplier_2_out));  // open: cin, cout
  Multiplier #(.width(32)) multiplier_3 (.a(in_1), .b(in_6), .out(multiplier_3_out));  // open: cin, cout
  Multiplier #(.width(32)) multiplier_4 (.a(in_2), .b(in_8), .out(multiplier_4_out));  // open: cin, cout
  Multiplier #(.width(32)) multiplier_5 (.a(in_3), .b(in_5), .out(multiplier_5_out));  // open: cin, cout
  Multiplier #(.width(32)) multiplier_6 (.a(in_4), .b(in_7), .out(multiplier_6_out));  // open: cin, cout
  Multiplier #(.width(32)) multiplier_7 (.a(in_3), .b(in_6), .out(multiplier_7_out));  // open: cin, cout
  Multiplier #(.width(32)) multiplier_8 (.a(in_4), .b(in_8), .out(multiplier_8_out));  // open: cin, cout
  Adder #(.width(32)) adder_1 (.a(multiplier_1_out), .b(multiplier_2_out), .out(out_9));  // open: cin, cout
  Adder #(.width(32)) adder_2 (.a(multiplier_3_out), .b(multiplier_4_out), .out(out_10));  // open: cin, cout
  Adder #(.width(32)) adder_3 (.a(multiplier_5_out), .b(multiplier_6_out), .out(out_11));  // open: cin, cout
  Adder #(.width(32)) adder_4 (.a(multiplier_7_out), .b(multiplier_8_out), .out(out_12));  // open: cin, cout
endmodule

module \矩阵select  (
  input  [31:0] in_1,
  input  [31:0] in_2,
  input  [31:0] in_3,
  input  [31:0] in_4,
  input  [31:0] in_5,
  input  [31:0] in_6,
  input  [31:0] in_7,
  input  [31:0] in_8,
  input  selector,
  output [31:0] out_10,
  output [31:0] out_11,
  output [31:0] out_12,
  output [31:0] out_13
);

  Multiplexer #(.width(32)) multiplexer_1 (.in0(in_1), .in1(in_5), .out(out_10), .sel(selector));  // open: en
  Multiplexer #(.width(32)) multiplexer_2 (.in0(in_2), .in1(in_6), .out(out_11), .sel(selector));  // open: en
  Multiplexer #(.width(32)) multiplexer_3 (.in0(in_3), .in1(in_7), .out(out_12), .sel(selector));  // open: en
  Multiplexer #(.width(32)) multiplexer_4 (.in0(in_4), .in1(in_8), .out(out_13), .sel(selector));  // open: en
endmodule

module \初始值one  (
  output [31:0] out_1,
  output [31:0] out_2,
  output [31:0] out_3,
  output [31:0] out_4
);


  assign out_1 = 32'h1;
  assign out_2 = 32'h1;
  assign out_3 = 32'h1;
  assign out_4 = {32{1'b0}};
endmodule

module \单位  (
  output [31:0] out_1,
  output [31:0] out_2,
  output [31:0] out_3,
  output [31:0] out_4
);


  assign out_1 = 32'h1;
  assign out_2 = {32{1'b0}};
  assign out_3 = {32{1'b0}};
  assign out_4 = 32'h1;
endmodule

module \计算  (
  input  in_1,
  input  in_2,
  output [31:0] out_3
);

  wire clk, init, not_1_out;
  wire [31:0] multi_1_out_9, multi_1_out_10, multi_1_out_11, multi_1_out_12, \初始值one_1_out_1 ,
       \初始值one_1_out_2 , \初始值one_1_out_3 , \初始值one_1_out_4 , \单位_1_out_1 , \单位_1_out_2 , \单位_1_out_3 ,
       \单位_1_out_4 , \单位_2_out_1 , \单位_2_out_2 , \单位_2_out_3 , \单位_2_out_4 , \寄存器矩阵_1_a11_out ,
       \寄存器矩阵_1_a12_out , \寄存器矩阵_1_a21_out , \寄存器矩阵_1_a22_out , \寄存器矩阵_2_a11_out , \寄存器矩阵_2_a12_out ,
       \寄存器矩阵_2_a21_out , \寄存器矩阵_2_a22_out , \矩阵mul_out_9 , \矩阵mul_out_10 , \矩阵mul_out_11 , \矩阵mul_out_12 ,
       \矩阵select_1_out_10 , \矩阵select_1_out_11 , \矩阵select_1_out_12 , \矩阵select_1_out_13 ,
       \矩阵select_2_out_10 , \矩阵select_2_out_11 , \矩阵select_2_out_12 , \矩阵select_2_out_13 ,
       \矩阵select_3_out_10 , \矩阵select_3_out_11 , \矩阵select_3_out_12 , \矩阵select_3_out_13 ;

  Clock clock_1 (.out(clk));
  Counter #(.width(1), .max('h1), .ongoal("stay")) counter_1 (.Q(init), .clk(clk));  // open: load, D, count, carry, clr
  \单位  \u_单位_1  (.out_1(\单位_1_out_1 ), .out_2(\单位_1_out_2 ), .out_3(\单位_1_out_3 ), .out_4(\单位_1_out_4 ));
  multi \u_矩阵mul  (
    .in_1(\寄存器矩阵_1_a11_out ), .in_2(\寄存器矩阵_1_a12_out ), .in_3(\寄存器矩阵_1_a21_out ), .in_4(\寄存器矩阵_1_a22_out ),
    .in_5(\寄存器矩阵_1_a11_out ), .in_6(\寄存器矩阵_1_a12_out ), .in_7(\寄存器矩阵_1_a21_out ), .in_8(\寄存器矩阵_1_a22_out ),
    .out_9(\矩阵mul_out_9 ), .out_10(\矩阵mul_out_10 ), .out_11(\矩阵mul_out_11 ), .out_12(\矩阵mul_out_12 ));
  \矩阵select  \u_矩阵select_1  (
    .in_1(\单位_1_out_1 ), .in_2(\单位_1_out_2 ), .in_3(\单位_1_out_3 ), .in_4(\单位_1_out_4 ),
    .in_5(\寄存器矩阵_1_a11_out ), .in_6(\寄存器矩阵_1_a12_out ), .in_7(\寄存器矩阵_1_a21_out ), .in_8(\寄存器矩阵_1_a22_out ),
    .selector(in_1), .out_10(\矩阵select_1_out_10 ), .out_11(\矩阵select_1_out_11 ),
    .out_12(\矩阵select_1_out_12 ), .out_13(\矩阵select_1_out_13 ));
  \初始值one  \u_初始值one_1  (
    .out_1(\初始值one_1_out_1 ), .out_2(\初始值one_1_out_2 ), .out_3(\初始值one_1_out_3 ), .out_4(\初始值one_1_out_4 ));
  not not_1 (not_1_out, in_2);
  \单位  \u_单位_2  (.out_1(\单位_2_out_1 ), .out_2(\单位_2_out_2 ), .out_3(\单位_2_out_3 ), .out_4(\单位_2_out_4 ));
  \矩阵select  \u_矩阵select_2  (
    .in_1(\初始值one_1_out_1 ), .in_2(\初始值one_1_out_2 ), .in_3(\初始值one_1_out_3 ), .in_4(\初始值one_1_out_4 ),
    .in_5(\矩阵mul_out_9 ), .in_6(\矩阵mul_out_10 ), .in_7(\矩阵mul_out_11 ), .in_8(\矩阵mul_out_12 ),
    .selector(init), .out_10(\矩阵select_2_out_10 ), .out_11(\矩阵select_2_out_11 ),
    .out_12(\矩阵select_2_out_12 ), .out_13(\矩阵select_2_out_13 ));
  multi multi_1 (
    .in_1(\寄存器矩阵_2_a11_out ), .in_2(\寄存器矩阵_2_a12_out ), .in_3(\寄存器矩阵_2_a21_out ), .in_4(\寄存器矩阵_2_a22_out ),
    .in_5(\矩阵select_1_out_10 ), .in_6(\矩阵select_1_out_11 ), .in_7(\矩阵select_1_out_12 ),
    .in_8(\矩阵select_1_out_13 ), .out_9(multi_1_out_9), .out_10(multi_1_out_10), .out_11(multi_1_out_11),
    .out_12(multi_1_out_12));
  \寄存器矩阵  \u_寄存器矩阵_1  (
    .a11_in(\矩阵select_2_out_10 ), .a12_in(\矩阵select_2_out_11 ), .a13_in(\矩阵select_2_out_12 ),
    .a14_in(\矩阵select_2_out_13 ), .ena(not_1_out), .clk(clk), .a11_out(\寄存器矩阵_1_a11_out ),
    .a12_out(\寄存器矩阵_1_a12_out ), .a21_OUT(\寄存器矩阵_1_a21_out ), .a22_out(\寄存器矩阵_1_a22_out ));
  \矩阵select  \u_矩阵select_3  (
    .in_1(\单位_2_out_1 ), .in_2(\单位_2_out_2 ), .in_3(\单位_2_out_3 ), .in_4(\单位_2_out_4 ), .in_5(multi_1_out_9),
    .in_6(multi_1_out_10), .in_7(multi_1_out_11), .in_8(multi_1_out_12), .selector(init),
    .out_10(\矩阵select_3_out_10 ), .out_11(\矩阵select_3_out_11 ), .out_12(\矩阵select_3_out_12 ),
    .out_13(\矩阵select_3_out_13 ));
  \寄存器矩阵  \u_寄存器矩阵_2  (
    .a11_in(\矩阵select_3_out_10 ), .a12_in(\矩阵select_3_out_11 ), .a13_in(\矩阵select_3_out_12 ),
    .a14_in(\矩阵select_3_out_13 ), .ena(not_1_out), .clk(clk), .a11_out(\寄存器矩阵_2_a11_out ),
    .a12_out(\寄存器矩阵_2_a12_out ), .a21_OUT(\寄存器矩阵_2_a21_out ), .a22_out(\寄存器矩阵_2_a22_out ));
  Multiplexer #(.width(32)) multiplexer_1 (
    .in0({32{1'b0}}), .in1(\寄存器矩阵_2_a12_out ), .out(out_3), .sel(in_2));  // open: en
endmodule

module \计数  (
  input  [31:0] in_1,
  output out_2,
  output out_3
);

  wire clock_1_out, comparator_1_eq, counter_1_q;
  wire [31:0] multiplexer_1_out, register_1_q, shifter_1_out;

  Clock clock_1 (.out(clock_1_out));
  Counter #(.width(1), .max('h1), .ongoal("stay")) counter_1 (
    .Q(counter_1_q), .clk(clock_1_out));  // open: load, D, count, carry, clr
  Shifter #(.width(32), .shift("lr")) shifter_1 (.in(register_1_q), .\dist (5'b00001), .out(shifter_1_out));
  Comparator #(.width(32), .mode("unsigned")) comparator_1 (
    .a(register_1_q), .b({32{1'b0}}), .eq(comparator_1_eq));  // open: gt, lt
  Multiplexer #(.width(32)) multiplexer_1 (
    .in0(in_1), .in1(shifter_1_out), .out(multiplexer_1_out), .sel(counter_1_q));  // open: en
  Register #(.width(32)) register_1 (.D(multiplexer_1_out), .Q(register_1_q), .clk(clock_1_out));  // open: en, clr
  Bit_Extender #(.in_width(32), .out_width(1)) bit_extender_1 (.in(register_1_q), .out(out_2));
  Multiplexer multiplexer_2 (.in0(1'b0), .in1(comparator_1_eq), .out(out_3), .sel(counter_1_q));  // open: en
endmodule
