// Logisim project ftoi.circ as structural Verilog: 1 circuit, main circuit ftoi
module ftoi (
  input  [15:0] in_1,
  output [31:0] out_2
);

  wire comparator_1_lt, comparator_2_eq, comparator_3_eq, comparator_4_gt, or_1_out;
  wire [4:0] subtractor_1_out, subtractor_2_out, subtractor_3_out;
  wire [31:0] adder_1_out, adder_2_out, multiplexer_1_out, multiplexer_2_out, not_1_out, or_2_out,
       shifter_1_out, shifter_2_out, shifter_3_out;

  Comparator #(.width(5), .mode("unsigned")) comparator_1 (
    .a(in_1[14:10]), .b(5'b01111), .lt(comparator_1_lt));  // open: gt, eq
  Comparator #(.width(5), .mode("unsigned")) comparator_2 (
    .a(in_1[14:10]), .b({5{1'b1}}), .eq(comparator_2_eq));  // open: gt, lt
  Comparator #(.width(5)) comparator_3 (.a(in_1[14:10]), .b({5{1'b0}}), .eq(comparator_3_eq));  // open: gt, lt
  // Probe on subtractor_1_out
  Subtractor #(.width(5)) subtractor_1 (.a(in_1[14:10]), .b(5'b01111), .out(subtractor_1_out));  // open: bin, bout
  or or_1 (or_1_out, comparator_2_eq, comparator_1_lt, comparator_3_eq);
  Subtractor #(.width(5)) subtractor_2 (.a(subtractor_1_out), .b(5'b01010), .out(subtractor_2_out));  // open: bin, bout
  Shifter #(.width(32), .shift("lr")) shifter_1 (
    .in({{22{1'b0}}, in_1[9:0]}), .\dist (subtractor_3_out), .out(shifter_1_out));
  // Probe on shifter_2_out
  Shifter #(.width(32)) shifter_2 (.in(32'h1), .\dist (subtractor_1_out), .out(shifter_2_out));
  Subtractor #(.width(5)) subtractor_3 (.a(5'b01010), .b(subtractor_1_out), .out(subtractor_3_out));  // open: bin, bout
  Shifter #(.width(32)) shifter_3 (.in({{22{1'b0}}, in_1[9:0]}), .\dist (subtractor_2_out), .out(shifter_3_out));
  Multiplexer #(.width(32)) multiplexer_1 (
    .in0(shifter_3_out), .in1(shifter_1_out), .out(multiplexer_1_out), .sel(comparator_4_gt));  // open: en
  Adder #(.width(32)) adder_1 (.a(shifter_2_out), .b(multiplexer_1_out), .out(adder_1_out));  // open: cin, cout
  Comparator #(.width(5)) comparator_4 (.a(subtractor_3_out), .b({5{1'b0}}), .gt(comparator_4_gt));  // open: eq, lt
  assign not_1_out = ~adder_1_out;  // NOT_Gate not_1, 32 bits wide
  Adder #(.width(32)) adder_2 (.a(not_1_out), .b(32'h1), .out(adder_2_out));  // open: cin, cout
  Multiplexer #(.width(32)) multiplexer_2 (
    .in0(adder_1_out), .in1(or_2_out), .out(multiplexer_2_out), .sel(in_1[15]));  // open: en
  Multiplexer #(.width(32)) multiplexer_3 (
    .in0(multiplexer_2_out), .in1({32{1'b0}}), .out(out_2), .sel(or_1_out));  // open: en
  assign or_2_out = adder_2_out | {in_1[15], {31{1'b0}}};  // OR_Gate or_2, 32 bits wide

  // Other names for the same wires on the sheet: _0 = in_1[0]; _1 = in_1[1]; _2 = in_1[2]; _3 = in_1[3]; _4 = in_1[4];
  //   _5 = in_1[5]; _6 = in_1[6]; _7 = in_1[7]; _8 = in_1[8]; _9 = in_1[9]
endmodule
