// Logisim project grf.circ as structural Verilog: 1 circuit, main circuit grf
module grf (
  input  in_1,
  input  in_2,
  input  WE,
  input  [4:0] in_4,
  input  [4:0] in_5,
  input  [4:0] in_6,
  input  [31:0] in_7,
  output [31:0] out_8,
  output [31:0] out_9
);

  wire [31:0] _0, _0_t, _1, _1_t, _2, _2_t, _3, _3_t, _4, _4_t, _5, _5_t, _6, _6_t, _7, _7_t, _8, _8_t, _9,
       _9_t, _10, _10_t, _11, _11_t, _12, _12_t, _13, _13_t, _14, _14_t, _15, _15_t, _16, _16_t, _17, _17_t,
       _18, _18_t, _19, _19_t, _20, _20_t, _21, _21_t, _22, _22_t, _23, _23_t, _24, _24_t, _25, _25_t, _26,
       _26_t, _27, _27_t, _28, _28_t, _29, _29_t, _30, _30_t, _31, _31_t;

  Demultiplexer #(.select(5), .width(32), .tristate("true")) demultiplexer_1 (
    .out0(_0), .out1(_1), .out2(_2), .out3(_3), .out4(_4), .out5(_5), .out6(_6), .out7(_7), .out8(_8),
    .out9(_9), .out10(_10), .out11(_11), .out12(_12), .out13(_13), .out14(_14), .out15(_15), .out16(_16),
    .out17(_17), .out18(_18), .out19(_19), .out20(_20), .out21(_21), .out22(_22), .out23(_23), .out24(_24),
    .out25(_25), .out26(_26), .out27(_27), .out28(_28), .out29(_29), .out30(_30), .out31(_31), .in(in_7),
    .sel(in_6), .en(WE));
  Register #(.width(32)) register_1 (.D(_0), .Q(_0_t), .clk(in_1), .clr(1'b1));  // open: en
  Register #(.width(32)) register_2 (.D(_4), .Q(_4_t), .clk(in_1), .clr(in_2));  // open: en
  Register #(.width(32)) register_3 (.D(_8), .Q(_8_t), .clk(in_1), .clr(in_2));  // open: en
  Register #(.width(32)) register_4 (.D(_12), .Q(_12_t), .clk(in_1), .clr(in_2));  // open: en
  Register #(.width(32)) register_5 (.D(_16), .Q(_16_t), .clk(in_1), .clr(in_2));  // open: en
  Register #(.width(32)) register_6 (.D(_20), .Q(_20_t), .clk(in_1), .clr(in_2));  // open: en
  Register #(.width(32)) register_7 (.D(_24), .Q(_24_t), .clk(in_1), .clr(in_2));  // open: en
  Register #(.width(32)) register_8 (.D(_28), .Q(_28_t), .clk(in_1), .clr(in_2));  // open: en
  Register #(.width(32)) register_9 (.D(_1), .Q(_1_t), .clk(in_1), .clr(in_2));  // open: en
  Register #(.width(32)) register_10 (.D(_5), .Q(_5_t), .clk(in_1), .clr(in_2));  // open: en
  Register #(.width(32)) register_11 (.D(_9), .Q(_9_t), .clk(in_1), .clr(in_2));  // open: en
  Register #(.width(32)) register_12 (.D(_13), .Q(_13_t), .clk(in_1), .clr(in_2));  // open: en
  Register #(.width(32)) register_13 (.D(_17), .Q(_17_t), .clk(in_1), .clr(in_2));  // open: en
  Register #(.width(32)) register_14 (.D(_21), .Q(_21_t), .clk(in_1), .clr(in_2));  // open: en
  Register #(.width(32)) register_15 (.D(_25), .Q(_25_t), .clk(in_1), .clr(in_2));  // open: en
  Register #(.width(32)) register_16 (.D(_29), .Q(_29_t), .clk(in_1), .clr(in_2));  // open: en
  Register #(.width(32)) register_17 (.D(_2), .Q(_2_t), .clk(in_1), .clr(in_2));  // open: en
  Register #(.width(32)) register_18 (.D(_6), .Q(_6_t), .clk(in_1), .clr(in_2));  // open: en
  Register #(.width(32)) register_19 (.D(_10), .Q(_10_t), .clk(in_1), .clr(in_2));  // open: en
  Register #(.width(32)) register_20 (.D(_14), .Q(_14_t), .clk(in_1), .clr(in_2));  // open: en
  Register #(.width(32)) register_21 (.D(_18), .Q(_18_t), .clk(in_1), .clr(in_2));  // open: en
  Register #(.width(32)) register_22 (.D(_22), .Q(_22_t), .clk(in_1), .clr(in_2));  // open: en
  Register #(.width(32)) register_23 (.D(_26), .Q(_26_t), .clk(in_1), .clr(in_2));  // open: en
  Register #(.width(32)) register_24 (.D(_30), .Q(_30_t), .clk(in_1), .clr(in_2));  // open: en
  Register #(.width(32)) register_25 (.D(_3), .Q(_3_t), .clk(in_1), .clr(in_2));  // open: en
  Register #(.width(32)) register_26 (.D(_7), .Q(_7_t), .clk(in_1), .clr(in_2));  // open: en
  Register #(.width(32)) register_27 (.D(_11), .Q(_11_t), .clk(in_1), .clr(in_2));  // open: en
  Register #(.width(32)) register_28 (.D(_15), .Q(_15_t), .clk(in_1), .clr(in_2));  // open: en
  Register #(.width(32)) register_29 (.D(_19), .Q(_19_t), .clk(in_1), .clr(in_2));  // open: en
  Register #(.width(32)) register_30 (.D(_23), .Q(_23_t), .clk(in_1), .clr(in_2));  // open: en
  Register #(.width(32)) register_31 (.D(_27), .Q(_27_t), .clk(in_1), .clr(in_2));  // open: en
  Register #(.width(32)) register_32 (.D(_31), .Q(_31_t), .clk(in_1), .clr(in_2));  // open: en
  Multiplexer #(.select(5), .width(32), .enable("false")) multiplexer_1 (
    .in0(_0_t), .in1(_1_t), .in2(_2_t), .in3(_3_t), .in4(_4_t), .in5(_5_t), .in6(_6_t), .in7(_7_t),
    .in8(_8_t), .in9(_9_t), .in10(_10_t), .in11(_11_t), .in12(_12_t), .in13(_13_t), .in14(_14_t),
    .in15(_15_t), .in16(_16_t), .in17(_17_t), .in18(_18_t), .in19(_19_t), .in20(_20_t), .in21(_21_t),
    .in22(_22_t), .in23(_23_t), .in24(_24_t), .in25(_25_t), .in26(_26_t), .in27(_27_t), .in28(_28_t),
    .in29(_29_t), .in30(_30_t), .in31(_31_t), .out(out_8), .sel(in_4));
  Multiplexer #(.select(5), .width(32), .enable("false")) multiplexer_2 (
    .in0(_0_t), .in1(_1_t), .in2(_2_t), .in3(_3_t), .in4(_4_t), .in5(_5_t), .in6(_6_t), .in7(_7_t),
    .in8(_8_t), .in9(_9_t), .in10(_10_t), .in11(_11_t), .in12(_12_t), .in13(_13_t), .in14(_14_t),
    .in15(_15_t), .in16(_16_t), .in17(_17_t), .in18(_18_t), .in19(_19_t), .in20(_20_t), .in21(_21_t),
    .in22(_22_t), .in23(_23_t), .in24(_24_t), .in25(_25_t), .in26(_26_t), .in27(_27_t), .in28(_28_t),
    .in29(_29_t), .in30(_30_t), .in31(_31_t), .out(out_9), .sel(in_5));

  // Other names for the same wires on the sheet: clk = in_1; reset = in_2
endmodule
