// Logisim project mod.circ as structural Verilog
module Trans (
  input  S1,
  input  S2,
  input  In,
  output S1_prime,
  output S2_prime
);

  wire and_1_out, and_2_out, and_3_out, and_4_out, and_5_out, and_6_out, not_1_out, not_2_out, not_3_out,
       not_4_out, not_5_out, not_6_out, not_7_out, not_8_out;

  not not_1 (not_1_out, S1);
  not not_2 (not_2_out, S2);
  not not_3 (not_3_out, S1);
  not not_4 (not_4_out, S2);
  not not_5 (not_5_out, S1);
  not not_6 (not_6_out, In);
  not not_7 (not_7_out, S2);
  not not_8 (not_8_out, In);
  and and_1 (and_1_out, not_1_out, S2);
  and and_2 (and_2_out, S1, not_2_out);
  and and_3 (and_3_out, not_3_out, not_4_out, In);
  and and_4 (and_4_out, not_5_out, S2, not_6_out);
  and and_5 (and_5_out, S1, not_7_out, not_8_out);
  and and_6 (and_6_out, S1, S2, In);
  or or_1 (S1_prime, and_1_out, and_2_out);
  or or_2 (S2_prime, and_3_out, and_4_out, and_5_out, and_6_out);
endmodule

module mod5 (
  input  in_1,
  output out_2,
  output out_3,
  output out_4,
  output out_5,
  output out_6
);

  wire clock_1_out;
  wire [1:0] register_1_q, trans_1_s1_prime;

  Trans trans_1 (
    .S1(register_1_q[0]), .S2(register_1_q[1]), .In(in_1), .S1_prime(trans_1_s1_prime[0]),
    .S2_prime(trans_1_s1_prime[1]));
  Clock clock_1 (.out(clock_1_out));
  Register #(.width(2)) register_1 (.D(trans_1_s1_prime), .Q(register_1_q), .clk(clock_1_out));  // open: en, clr
  Out out_1 (.S1(register_1_q[0]), .S2(register_1_q[1]), .In(in_1), .O1(out_3), .O2(out_4), .O3(out_5), .O4(out_6));

  assign out_2 = 1'b0;
endmodule

module Out (
  input  S1,
  input  S2,
  input  In,
  output O1,
  output O2,
  output O3,
  output O4
);

  wire and_1_out, and_2_out, and_3_out, and_4_out, and_5_out, and_6_out, and_7_out, and_8_out, not_1_out,
       not_2_out, not_3_out, not_4_out, not_5_out, not_6_out, not_7_out, not_8_out, not_9_out, not_10_out,
       not_11_out, not_12_out;

  not not_1 (not_1_out, S1);
  not not_2 (not_2_out, S2);
  not not_3 (not_3_out, In);
  not not_4 (not_4_out, In);
  not not_5 (not_5_out, S1);
  not not_6 (not_6_out, S2);
  not not_7 (not_7_out, S1);
  not not_8 (not_8_out, S2);
  not not_9 (not_9_out, S1);
  not not_10 (not_10_out, In);
  not not_11 (not_11_out, S2);
  not not_12 (not_12_out, In);
  and and_1 (and_1_out, not_1_out, not_2_out, not_3_out);
  and and_2 (and_2_out, S1, S2, not_4_out);
  and and_3 (and_3_out, not_5_out, not_6_out, In);
  and and_4 (and_4_out, S1, S2, In);
  and and_5 (and_5_out, not_7_out, S2, In);
  and and_6 (and_6_out, S1, not_8_out, In);
  and and_7 (and_7_out, not_9_out, S2, not_10_out);
  and and_8 (and_8_out, S1, not_11_out, not_12_out);
  or or_1 (O1, and_1_out, and_2_out);
  or or_2 (O2, and_3_out, and_4_out);
  or or_3 (O3, and_5_out, and_6_out);
  or or_4 (O4, and_7_out, and_8_out);
endmodule
