// Logisim project navigation.circ as structural Verilog: 4 circuits, main circuit navigation
module navigation (
  input  [1:0] in_1,
  input  in_2,
  input  in_3,
  output out_4,
  output out_5
);

  wire [3:0] register_1_q, \状态转移_1_out0 ;

  \状态转移  \u_状态转移_1  (
    .in1(in_1[1]), .in0(in_1[0]), .s3(register_1_q[3]), .s2(register_1_q[2]), .s1(register_1_q[1]),
    .s0(register_1_q[0]), .out3(\状态转移_1_out0 [3]), .out2(\状态转移_1_out0 [2]), .out1(\状态转移_1_out0 [1]),
    .out0(\状态转移_1_out0 [0]));
  Register #(.width(4)) register_1 (.D(\状态转移_1_out0 ), .Q(register_1_q), .clk(in_2), .clr(in_3));  // open: en
  \状态输出  \u_状态输出_1  (
    .s3(register_1_q[3]), .s2(register_1_q[2]), .s1(register_1_q[1]), .s0(register_1_q[0]), .hit(out_5),
    .arrive(out_4));
endmodule

module \状态转移  (
  input  in1,
  input  in0,
  input  s3,
  input  s2,
  input  s1,
  input  s0,
  output out3,
  output out2,
  output out1,
  output out0
);

  wire and_1_out, and_2_out, and_3_out, and_4_out, and_5_out, and_6_out, and_7_out, and_8_out, and_9_out,
       and_10_out, and_11_out, and_12_out, and_13_out, and_14_out, and_15_out, and_16_out, and_17_out,
       not_1_out, not_2_out, not_3_out, not_4_out, not_5_out, not_6_out, not_7_out, not_8_out, not_9_out,
       not_10_out, not_11_out, not_12_out, not_13_out, not_14_out, not_15_out, not_16_out, not_17_out,
       not_18_out, not_19_out, not_20_out, not_21_out, not_22_out, not_23_out, not_24_out, not_25_out,
       not_26_out, not_27_out, not_28_out;

  not not_1 (not_1_out, in1);
  not not_2 (not_2_out, in0);
  not not_3 (not_3_out, s1);
  not not_4 (not_4_out, in1);
  not not_5 (not_5_out, in1);
  not not_6 (not_6_out, in0);
  not not_7 (not_7_out, in1);
  not not_8 (not_8_out, s2);
  not not_9 (not_9_out, in1);
  not not_10 (not_10_out, s1);
  not not_11 (not_11_out, in0);
  not not_12 (not_12_out, s1);
  not not_13 (not_13_out, in1);
  not not_14 (not_14_out, in0);
  not not_15 (not_15_out, s3);
  not not_16 (not_16_out, s2);
  not not_17 (not_17_out, in0);
  not not_18 (not_18_out, in1);
  not not_19 (not_19_out, in0);
  not not_20 (not_20_out, in1);
  not not_21 (not_21_out, s3);
  not not_22 (not_22_out, s1);
  not not_23 (not_23_out, s3);
  not not_24 (not_24_out, s2);
  not not_25 (not_25_out, s1);
  not not_26 (not_26_out, in0);
  not not_27 (not_27_out, s3);
  not not_28 (not_28_out, s1);
  and and_1 (and_1_out, not_1_out, not_2_out, s2, not_3_out);
  and and_2 (and_2_out, s3, s0);
  and and_3 (and_3_out, not_4_out, in0, s2, s1);
  and and_4 (and_4_out, not_5_out, not_6_out, s1);
  and and_5 (and_5_out, not_7_out, not_8_out, s1);
  and and_6 (and_6_out, not_9_out, in0, s2, not_10_out);
  and and_7 (and_7_out, in1, not_11_out, s2, not_12_out);
  and and_8 (and_8_out, in1, in0, s2, s1);
  and and_9 (and_9_out, not_13_out, not_14_out, not_15_out, not_16_out);
  and and_10 (and_10_out, not_17_out, s2, s1);
  and and_11 (and_11_out, in1, in0, s1);
  and and_12 (and_12_out, in1, in0, s2);
  and and_13 (and_13_out, not_18_out, not_19_out, s2, s1);
  and and_14 (and_14_out, not_20_out, in0, not_21_out, not_22_out);
  and and_15 (and_15_out, in0, not_23_out, not_24_out, not_25_out);
  and and_16 (and_16_out, in1, not_26_out, not_27_out, not_28_out);
  and and_17 (and_17_out, in1, in0, s1);
  or or_1 (out3, and_1_out, and_2_out, and_3_out);
  or or_2 (out2, and_4_out, and_5_out, and_6_out, and_7_out, and_8_out);
  or or_3 (out1, and_9_out, and_10_out, and_11_out, and_12_out);
  or or_4 (out0, and_13_out, and_14_out, and_15_out, and_16_out, and_17_out);
endmodule

module \状态输出  (
  input  s3,
  input  s2,
  input  s1,
  input  s0,
  output hit,
  output arrive
);


  assign arrive = s3;
  assign hit = s0;
endmodule

module \状态输出_2  (
  input  s3,
  input  s2,
  input  s1,
  input  s0,
  output hit,
  output arrive
);

  wire not_1_out, not_2_out, not_3_out, not_4_out;

  not not_1 (not_1_out, s3);
  and and_1 (hit, not_1_out, s0);
  not not_2 (not_2_out, s2);
  not not_3 (not_3_out, s1);
  not not_4 (not_4_out, s0);
  and and_2 (arrive, s3, not_2_out, not_3_out, not_4_out);
endmodule
