// Logisim project p3-单周期cpu.circ as structural Verilog: 9 circuits, main circuit main
module main (
  input  Reset,
  output [31:0] out_2,
  output out_3,
  output [4:0] out_4,
  output [31:0] out_5,
  output out_6,
  output [4:0] out_7,
  output [31:0] out_8
);

  wire clock_1_out, clock_2_out, ExtOp, zero;
  wire [2:0] ALUOp, M1sel, M2sel, M3sel, NPCOp;
  wire [4:0] _15_11, _20_16, _25_21, shamt;
  wire [5:0] func, opcod;
  wire [15:0] splitter_1_imm;
  wire [25:0] address;
  wire [31:0] ALUre, DMdata, Ext, IFU_out_4, luire, npc_1_out, PC_4, RD1, shifter_2_out, SrcB;

  // Probe on out_2
  // Probe on IFU_out_4
  IFU IFU (.in_1(npc_1_out), .in_2(Reset), .out_3(out_2), .out_4(IFU_out_4));
  NPC npc_1 (.in_1(NPCOp), .out(npc_1_out), .im(address), .ra(RD1), .zero(zero), .PC4(PC_4), .PC(IFU_out_4));
  splitter splitter_1 (
    .in_1(out_2), .func(func), ._15_11(_15_11), ._20_16(_20_16), ._25_21(_25_21), .opcode(opcod),
    .shamt(shamt), .imm(splitter_1_imm), .address(address));
  // Probe on nothing
  Multiplexer #(.select(3), .width(5), .enable("false")) multiplexer_1 (
    .in0(_15_11), .in1(_20_16), .in2({5{1'b1}}), .out(out_4), .sel(M1sel));  // open: in3, in4, in5, in6, in7
  Multiplexer #(.select(3), .width(32), .enable("false")) multiplexer_2 (
    .in0(out_8), .in1(Ext), .in2(luire), .out(SrcB), .sel(M3sel));  // open: in3, in4, in5, in6, in7
  Controler controler_1 (
    .opcode(opcod), .funct(func), .RfWr(out_3), .ExtOp(ExtOp), .DMWr(out_6), .ALUOp(ALUOp), .M1sel(M1sel),
    .M2sel(M2sel), .M3sel(M3sel), .NPCOp(NPCOp));
  Clock clock_1 (.out(clock_1_out));
  Extender extender_1 (.in_1(splitter_1_imm), .in_2(ExtOp), .out_3(Ext));
  grf grf_1 (
    .in_2(Reset), .WE(out_3), .in_4(_25_21), .in_5(_20_16), .in_6(out_4), .in_7(out_5), .out_8(RD1),
    .out_9(out_8), .in_1(clock_1_out));
  Multiplexer #(.select(3), .width(32), .enable("false")) multiplexer_3 (
    .in0(ALUre), .in1(DMdata), .in2(PC_4), .out(out_5), .sel(M2sel));  // open: in3, in4, in5, in6, in7
  Shifter #(.width(32)) shifter_1 (.in(Ext), .\dist (5'b10000), .out(luire));
  ALU alu_1 (.in_1(RD1), .in_2(SrcB), .in_3(ALUOp), .out_4(zero), .out_5(ALUre));
  Shifter #(.width(32), .shift("lr")) shifter_2 (.in(ALUre), .\dist (5'b00010), .out(shifter_2_out));
  // Probe on out_5
  Bit_Extender #(.in_width(32), .out_width(5)) bit_extender_1 (.in(shifter_2_out), .out(out_7));
  Clock clock_2 (.out(clock_2_out));
  RAM #(.addrWidth(5), .dataWidth(32), .bus("separate")) ram_1 (
    .addr(out_7), .din(out_8), .data(DMdata), .str(out_6), .clk(clock_2_out), .ld(1'b1), .clr(Reset));  // open: sel

  // Other names for the same wires on the sheet: Instr[31:0] = out_2; MemAddr[4:0] = out_7; MemWrite = out_6;
  //   RD2[31:0] = out_8; RegAddr[4:0] = out_4; RegData[31:0] = out_5; RegWrite = out_3
endmodule

module grf (
  input  in_1,
  input  in_2,
  input  WE,
  input  [4:0] in_4,
  input  [4:0] in_5,
  input  [4:0] in_6,
  input  [31:0] in_7,
  output [31:0] out_8,
  output [31:0] out_9
);

  wire [31:0] _0, _0_t, _1, _1_t, _2, _2_t, _3, _3_t, _4, _4_t, _5, _5_t, _6, _6_t, _7, _7_t, _8, _8_t, _9,
       _9_t, _10, _10_t, _11, _11_t, _12, _12_t, _13, _13_t, _14, _14_t, _15, _15_t, _16, _16_t, _17, _17_t,
       _18, _18_t, _19, _19_t, _20, _20_t, _21, _21_t, _22, _22_t, _23, _23_t, _24, _24_t, _25, _25_t, _26,
       _26_t, _27, _27_t, _28, _28_t, _29, _29_t, _30, _30_t, _31, _31_t;

  Demultiplexer #(.select(5), .width(32), .tristate("true")) demultiplexer_1 (
    .out0(_0), .out1(_1), .out2(_2), .out3(_3), .out4(_4), .out5(_5), .out6(_6), .out7(_7), .out8(_8),
    .out9(_9), .out10(_10), .out11(_11), .out12(_12), .out13(_13), .out14(_14), .out15(_15), .out16(_16),
    .out17(_17), .out18(_18), .out19(_19), .out20(_20), .out21(_21), .out22(_22), .out23(_23), .out24(_24),
    .out25(_25), .out26(_26), .out27(_27), .out28(_28), .out29(_29), .out30(_30), .out31(_31), .in(in_7),
    .sel(in_6), .en(WE));
  // Probe on nothing
  Register #(.width(32)) register_1 (.D(_0), .Q(_0_t), .clk(in_1), .clr(1'b1));  // open: en
  Register #(.width(32)) register_2 (.D(_4), .Q(_4_t), .clk(in_1), .clr(in_2));  // open: en
  Register #(.width(32)) register_3 (.D(_8), .Q(_8_t), .clk(in_1), .clr(in_2));  // open: en
  Register #(.width(32)) register_4 (.D(_12), .Q(_12_t), .clk(in_1), .clr(in_2));  // open: en
  Register #(.width(32)) register_5 (.D(_16), .Q(_16_t), .clk(in_1), .clr(in_2));  // open: en
  Register #(.width(32)) register_6 (.D(_20), .Q(_20_t), .clk(in_1), .clr(in_2));  // open: en
  Register #(.width(32)) register_7 (.D(_24), .Q(_24_t), .clk(in_1), .clr(in_2));  // open: en
  Register #(.width(32)) register_8 (.D(_28), .Q(_28_t), .clk(in_1), .clr(in_2));  // open: en
  Register #(.width(32)) register_9 (.D(_1), .Q(_1_t), .clk(in_1), .clr(in_2));  // open: en
  Register #(.width(32)) register_10 (.D(_5), .Q(_5_t), .clk(in_1), .clr(in_2));  // open: en
  Register #(.width(32)) register_11 (.D(_9), .Q(_9_t), .clk(in_1), .clr(in_2));  // open: en
  Register #(.width(32)) register_12 (.D(_13), .Q(_13_t), .clk(in_1), .clr(in_2));  // open: en
  Register #(.width(32)) register_13 (.D(_17), .Q(_17_t), .clk(in_1), .clr(in_2));  // open: en
  Register #(.width(32)) register_14 (.D(_21), .Q(_21_t), .clk(in_1), .clr(in_2));  // open: en
  Register #(.width(32)) register_15 (.D(_25), .Q(_25_t), .clk(in_1), .clr(in_2));  // open: en
  Register #(.width(32)) register_16 (.D(_29), .Q(_29_t), .clk(in_1), .clr(in_2));  // open: en
  Register #(.width(32)) register_17 (.D(_2), .Q(_2_t), .clk(in_1), .clr(in_2));  // open: en
  Register #(.width(32)) register_18 (.D(_6), .Q(_6_t), .clk(in_1), .clr(in_2));  // open: en
  Register #(.width(32)) register_19 (.D(_10), .Q(_10_t), .clk(in_1), .clr(in_2));  // open: en
  Register #(.width(32)) register_20 (.D(_14), .Q(_14_t), .clk(in_1), .clr(in_2));  // open: en
  Register #(.width(32)) register_21 (.D(_18), .Q(_18_t), .clk(in_1), .clr(in_2));  // open: en
  Register #(.width(32)) register_22 (.D(_22), .Q(_22_t), .clk(in_1), .clr(in_2));  // open: en
  Register #(.width(32)) register_23 (.D(_26), .Q(_26_t), .clk(in_1), .clr(in_2));  // open: en
  Register #(.width(32)) register_24 (.D(_30), .Q(_30_t), .clk(in_1), .clr(in_2));  // open: en
  Register #(.width(32)) register_25 (.D(_3), .Q(_3_t), .clk(in_1), .clr(in_2));  // open: en
  Register #(.width(32)) register_26 (.D(_7), .Q(_7_t), .clk(in_1), .clr(in_2));  // open: en
  Register #(.width(32)) register_27 (.D(_11), .Q(_11_t), .clk(in_1), .clr(in_2));  // open: en
  Register #(.width(32)) register_28 (.D(_15), .Q(_15_t), .clk(in_1), .clr(in_2));  // open: en
  Register #(.width(32)) register_29 (.D(_19), .Q(_19_t), .clk(in_1), .clr(in_2));  // open: en
  Register #(.width(32)) register_30 (.D(_23), .Q(_23_t), .clk(in_1), .clr(in_2));  // open: en
  Register #(.width(32)) register_31 (.D(_27), .Q(_27_t), .clk(in_1), .clr(in_2));  // open: en
  Register #(.width(32)) register_32 (.D(_31), .Q(_31_t), .clk(in_1), .clr(in_2));  // open: en
  Multiplexer #(.select(5), .width(32), .enable("false")) multiplexer_1 (
    .in0(_0_t), .in1(_1_t), .in2(_2_t), .in3(_3_t), .in4(_4_t), .in5(_5_t), .in6(_6_t), .in7(_7_t),
    .in8(_8_t), .in9(_9_t), .in10(_10_t), .in11(_11_t), .in12(_12_t), .in13(_13_t), .in14(_14_t),
    .in15(_15_t), .in16(_16_t), .in17(_17_t), .in18(_18_t), .in19(_19_t), .in20(_20_t), .in21(_21_t),
    .in22(_22_t), .in23(_23_t), .in24(_24_t), .in25(_25_t), .in26(_26_t), .in27(_27_t), .in28(_28_t),
    .in29(_29_t), .in30(_30_t), .in31(_31_t), .out(out_8), .sel(in_4));
  Multiplexer #(.select(5), .width(32), .enable("false")) multiplexer_2 (
    .in0(_0_t), .in1(_1_t), .in2(_2_t), .in3(_3_t), .in4(_4_t), .in5(_5_t), .in6(_6_t), .in7(_7_t),
    .in8(_8_t), .in9(_9_t), .in10(_10_t), .in11(_11_t), .in12(_12_t), .in13(_13_t), .in14(_14_t),
    .in15(_15_t), .in16(_16_t), .in17(_17_t), .in18(_18_t), .in19(_19_t), .in20(_20_t), .in21(_21_t),
    .in22(_22_t), .in23(_23_t), .in24(_24_t), .in25(_25_t), .in26(_26_t), .in27(_27_t), .in28(_28_t),
    .in29(_29_t), .in30(_30_t), .in31(_31_t), .out(out_9), .sel(in_5));

  // Other names for the same wires on the sheet: clk = in_1; reset = in_2
endmodule

module IFU (
  input  [31:0] in_1,
  input  in_2,
  output [31:0] out_3,
  output [31:0] out_4
);

  wire clock_1_out;
  wire [4:0] bit_extender_1_out;
  wire [31:0] shifter_1_out;

  Clock clock_1 (.out(clock_1_out));
  Register #(.width(32)) PC (.D(in_1), .Q(out_4), .clk(clock_1_out), .clr(in_2));  // open: en
  Shifter #(.width(32), .shift("lr")) shifter_1 (.in(out_4), .\dist (5'b00010), .out(shifter_1_out));
  Bit_Extender #(.in_width(32), .out_width(5)) bit_extender_1 (.in(shifter_1_out), .out(bit_extender_1_out));
  ROM #(.addrWidth(5), .dataWidth(32)) rom_1 (.addr(bit_extender_1_out), .data(out_3));  // open: sel

  // Notes on the sheet:
  //   contents of rom_1 (hex, n*v repeats v):
  //   34000000 34210001 34420002 34630003 34840004 34a50005 34c60006 34e70007 35080008 35290009 354a000a
  //   356b000b 358c000c 35ad000d 35ce000e 35ef000f 36100010 36310011 36520012 36730013 36940014 36b50015
  //   36d60016 36f70017 37180018 37390019 375a001a 377b001b 379c001c 37bd001d 37de001e 37ff001f
endmodule

module splitter (
  input  [31:0] in_1,
  output [5:0] func,
  output [4:0] _15_11,
  output [4:0] _20_16,
  output [4:0] _25_21,
  output [5:0] opcode,
  output [4:0] shamt,
  output [15:0] imm,
  output [25:0] address
);


  assign _15_11 = in_1[15:11];
  assign _20_16 = in_1[20:16];
  assign _25_21 = in_1[25:21];
  assign address = in_1[25:0];
  assign func = in_1[5:0];
  assign imm = in_1[15:0];
  assign opcode = in_1[31:26];
  assign shamt = in_1[10:6];
endmodule

module ALU (
  input  [31:0] in_1,
  input  [31:0] in_2,
  input  [2:0] in_3,
  output out_4,
  output [31:0] out_5
);

  wire [31:0] adder_1_out, or_1_out, subtractor_1_out;

  Adder #(.width(32)) adder_1 (.a(in_1), .b(in_2), .out(adder_1_out));  // open: cin, cout
  Subtractor #(.width(32)) subtractor_1 (.a(in_1), .b(in_2), .out(subtractor_1_out));  // open: bin, bout
  assign or_1_out = in_1 | in_2;  // OR_Gate or_1, 32 bits wide
  Comparator #(.width(32)) comparator_1 (.a(subtractor_1_out), .b({32{1'b0}}), .eq(out_4));  // open: gt, lt
  Multiplexer #(.select(3), .width(32), .enable("false")) multiplexer_1 (
    .in0(adder_1_out), .in1(subtractor_1_out), .in2(or_1_out), .out(out_5), .sel(in_3));  // open: in3, in4, in5, in6, in7
endmodule

module Controler (
  input  [5:0] opcode,
  input  [5:0] funct,
  output RfWr,
  output ExtOp,
  output DMWr,
  output [2:0] ALUOp,
  output [2:0] M1sel,
  output [2:0] M2sel,
  output [2:0] M3sel,
  output [2:0] NPCOp
);

  wire add, \and , beq, f0n, f1n, f2n, f3n, f4n, f5n, jal, jr, lui, lw, nop, op0n, op1n, op2n, op3n, op4n,
       op5n, ori, R_type, sub, sw;

  not not_1 (f0n, funct[0]);
  not not_2 (op0n, opcode[0]);
  not not_3 (op1n, opcode[1]);
  not not_4 (op2n, opcode[2]);
  not not_5 (op3n, opcode[3]);
  not not_6 (op4n, opcode[4]);
  not not_7 (op5n, opcode[5]);
  not not_8 (f1n, funct[1]);
  not not_9 (f2n, funct[2]);
  not not_10 (f3n, funct[3]);
  not not_11 (f4n, funct[4]);
  not not_12 (f5n, funct[5]);
  and u_sw (sw, opcode[5], op4n, opcode[3], op2n, opcode[1], opcode[0]);
  and u_beq (beq, op5n, op4n, op3n, opcode[2], op1n, op0n);
  and u_jal (jal, op5n, op4n, op3n, op2n, opcode[1], opcode[0]);
  and u_nop (nop, op5n, op4n, op3n, op2n, op1n, op0n);
  and and_1 (R_type, op0n, op1n, op2n, op3n, op4n, op5n);
  and u_add (add, R_type, funct[5], f4n, f3n, f2n, f1n, f0n);
  and u_sub (sub, R_type, funct[5], f4n, f3n, f2n, funct[1], f0n);
  and and_2 (\and , R_type, funct[5], f4n, f3n, funct[2], f1n, f0n);
  and u_ori (ori, op5n, op4n, opcode[3], opcode[2], op1n, opcode[0]);
  and u_lw (lw, opcode[5], op4n, op3n, op2n, opcode[1], opcode[0]);
  buf or_1 (M3sel[1], lui);  // OR_Gate
  or or_2 (ALUOp[0], sub, beq);
  buf or_3 (ALUOp[1], ori);  // OR_Gate
  or or_4 (NPCOp[1], jal, jr);
  and u_jr (jr, R_type, f5n, f4n, funct[3], f2n, f1n, f0n);
  and u_lui (lui, op5n, op4n, opcode[3], opcode[2], opcode[1], opcode[0]);
  or or_5 (M1sel[0], ori, lw, lui);
  buf or_6 (M2sel[0], lw);  // OR_Gate
  or or_7 (NPCOp[0], beq, jr);
  or or_8 (M3sel[0], ori, lw, sw);
  buf or_9 (M1sel[1], jal);  // OR_Gate
  buf or_10 (M2sel[1], jal);  // OR_Gate
  buf or_11 (M3sel[2], 1'b0);  // OR_Gate
  or or_12 (ExtOp, lw, sw);
  buf or_13 (DMWr, sw);  // OR_Gate
  buf or_14 (ALUOp[2], 1'b0);  // OR_Gate
  or or_15 (RfWr, add, sub, ori, lw, jal, lui);

  assign M1sel[2] = 1'b0;
  assign M2sel[2] = 1'b0;
  assign NPCOp[2] = 1'b0;

  // Other names for the same wires on the sheet: f0 = funct[0]; f1 = funct[1]; f2 = funct[2]; f3 = funct[3];
  //   f4 = funct[4]; f5 = funct[5]; M3s1 = M3sel[1]; op0 = opcode[0]; op1 = opcode[1]; op2 = opcode[2];
  //   op3 = opcode[3]; op4 = opcode[4]; op5 = opcode[5]
endmodule

module Extender (
  input  [15:0] in_1,
  input  in_2,
  output [31:0] out_3
);

  wire [31:0] bit_extender_1_out, bit_extender_2_out;

  assign bit_extender_1_out = {{16{1'b0}}, in_1};  // Bit_Extender bit_extender_1
  assign bit_extender_2_out = {{16{in_1[15]}}, in_1};  // Bit_Extender bit_extender_2
  Multiplexer #(.width(32), .enable("false")) multiplexer_1 (
    .in0(bit_extender_1_out), .in1(bit_extender_2_out), .out(out_3), .sel(in_2));
endmodule

module NPC (
  input  [2:0] in_1,
  input  [31:0] PC,
  input  [25:0] im,
  input  [31:0] ra,
  input  zero,
  output [31:0] out,
  output [31:0] PC4
);

  wire [15:0] bit_extender_1_out;
  wire [27:0] bit_extender_4_out;
  wire [31:0] adder_1_out, bit_extender_2_out, bit_extender_3_out, multiplexer_1_out, shifter_1_out,
       shifter_2_out;

  Bit_Extender #(.in_width(26)) bit_extender_1 (.in(im), .out(bit_extender_1_out));
  assign bit_extender_2_out = {{16{bit_extender_1_out[15]}}, bit_extender_1_out};  // Bit_Extender bit_extender_2
  Shifter #(.width(32)) shifter_1 (.in(bit_extender_2_out), .\dist (5'b00010), .out(shifter_1_out));
  assign bit_extender_3_out = {{6{im[25]}}, im};  // Bit_Extender bit_extender_3
  Adder #(.width(32)) adder_1 (.a(shifter_1_out), .b(PC4), .out(adder_1_out));  // open: cin, cout
  Shifter #(.width(32)) shifter_2 (.in(bit_extender_3_out), .\dist (5'b00010), .out(shifter_2_out));
  Bit_Extender #(.in_width(32), .out_width(28), .\type ("sign")) bit_extender_4 (
    .in(shifter_2_out), .out(bit_extender_4_out));
  Multiplexer #(.width(32), .enable("false")) multiplexer_1 (
    .in0(PC4), .in1(adder_1_out), .out(multiplexer_1_out), .sel(zero));
  Adder #(.width(32)) adder_2 (.a(PC), .b(32'h4), .out(PC4));  // open: cin, cout
  Multiplexer #(.select(3), .width(32), .enable("false")) multiplexer_2 (
    .in0(PC4), .in1(multiplexer_1_out), .in2({PC[31:28], bit_extender_4_out}), .in3(ra), .out(out), .sel(in_1));  // open: in4, in5, in6, in7

  // Other names for the same wires on the sheet: NPCOp[2:0] = in_1; PC28_31[3:0] = PC[31:28]; PC_4[31:0] = PC4
endmodule

module Load (
  input  [31:0] in_1,
  input  [31:0] in_2
);
endmodule
