// Logisim project zuoye1.circ as structural Verilog: 4 circuits, main circuit fsm
module fsm (
  input  in_1,
  input  [1:0] in_2,
  output out_3
);

  wire clock_1_out;
  wire [1:0] multiplexer_1_out, register_1_q, \状态转移_1_out_0 ;

  \状态转移  \u_状态转移_1  (
    .in_1(in_2[1]), .in_0(in_2[0]), .s1(register_1_q[1]), .s0(register_1_q[0]), .out_1(\状态转移_1_out_0 [1]),
    .out_0(\状态转移_1_out_0 [0]));
  Clock clock_1 (.out(clock_1_out));
  Multiplexer #(.width(2)) multiplexer_1 (
    .in0(\状态转移_1_out_0 ), .in1(2'b00), .out(multiplexer_1_out), .sel(in_1));  // open: en
  Register #(.width(2)) register_1 (.D(multiplexer_1_out), .Q(register_1_q), .clk(clock_1_out));  // open: en, clr
  \输出逻辑  \u_输出逻辑_1  (.in_1(in_2[1]), .in_0(in_2[0]), .s1(register_1_q[1]), .s0(register_1_q[0]), .z(out_3));

  // Other names for the same wires on the sheet: clr = in_1
endmodule

module \状态转移  (
  input  in_1,
  input  in_0,
  input  s1,
  input  s0,
  output out_1,
  output out_0
);

  wire and_1_out, and_2_out, and_3_out, and_4_out, not_1_out, not_2_out, not_3_out, not_4_out, not_5_out,
       not_6_out, not_7_out;

  not not_1 (not_1_out, in_0);
  not not_2 (not_2_out, s1);
  not not_3 (not_3_out, in_0);
  not not_4 (not_4_out, s0);
  not not_5 (not_5_out, in_0);
  not not_6 (not_6_out, s0);
  not not_7 (not_7_out, in_1);
  and and_1 (and_1_out, not_1_out, not_2_out, s0);
  and and_2 (and_2_out, not_3_out, s1, not_4_out);
  and and_3 (and_3_out, not_5_out, s1, not_6_out);
  and and_4 (and_4_out, not_7_out, in_0);
  or or_1 (out_1, and_1_out, and_2_out);
  or or_2 (out_0, and_3_out, and_4_out);
endmodule

module \输出逻辑  (
  input  in_1,
  input  in_0,
  input  s1,
  input  s0,
  output z
);

  wire not_1_out, not_2_out;

  not not_1 (not_1_out, in_0);
  not not_2 (not_2_out, s0);
  and and_1 (z, not_1_out, s1, not_2_out);
endmodule

module shuchu (
  input  in_1,
  input  in_0,
  input  s1,
  input  s0,
  output z
);

  wire not_1_out, not_2_out;

  not not_1 (not_1_out, in_0);
  and and_1 (z, not_1_out, s1, not_2_out);
  not not_2 (not_2_out, s0);
endmodule
